// Logisim project comp.circ as structural Verilog: 4 circuits, main circuit main
module main (
);

  wire A_In, A_Out, Addr_H_In, Addr_L_In, Addr_Out, ALU_C_In, ALU_C_Out, and_2_out, and_3_out, B_In, B_Out,
       BF, C_Clear, C_Set, CF, CF_En, CLK, clock_1_out, CNT_En, Cnt_H_In, Cnt_H_Out, Cnt_L_In, Cnt_L_Out,
       D_Clear, d_ff_1_q, d_ff_1_qn, D_Set, decoder_1_out0, decoder_1_out1, decoder_1_out2, decoder_4_out0,
       DF, F_In, F_Out, First_Select, HLT, I_Clear, I_Set, IF, Inst_In, LCF, Mic_RST, NF_En, nor_1_out,
       nor_3_out, not_1_out, not_2_out, or_1_out, or_2_out, or_3_out, or_4_out, P_Cnt_Lo_carry, SP_In,
       V_Clear, VF_En, Write, X_In, X_Out, Y_In, Y_Out, ZF_En;
  wire [1:0] Use_C_F;
  wire [2:0] ALU_Out_Select, Data_Out_Select, Flag_Inst, Second_Select;
  wire [3:0] Micro_q, OP_Select;
  wire [3:1] Condition;
  wire [6:0] keyboard_1_data;
  wire [7:0] A_Val, Addr_H_Val, Addr_L_Val, ALU_Out, B_Val, controlled_buffer_6_out, Data, Inst_q,
       multiplexer_1_out, multiplexer_4_out, P_Cnt_Hi_q, P_Cnt_Lo_q, random_1_out, SP_Val, X_Val, Y_Val;
  wire [7:1] nz_1_z;
  wire [7:7] keyboard_1_avail;
  wire [15:0] multiplexer_2_out;
  wire [31:29] rom_2_data;

  Clock clock_1 (.out(clock_1_out));
  D_Flip_Flop d_ff_1 (.clk(CLK), .D(d_ff_1_qn), .Q(d_ff_1_q), .Qn(d_ff_1_qn), .en(d_ff_1_qn));  // open: preset, reset
  and and_1 (CLK, clock_1_out, ~HLT);  // AND_Gate
  nor nor_1 (nor_1_out, multiplexer_2_out[14], multiplexer_2_out[15]);
  Register Addr_Lo (.D(ALU_Out), .en(Addr_L_In), .Q(Addr_L_Val), .clk(CLK));  // open: clr
  Counter #(.width(4), .max('hf), .trigger("falling")) Micro (
    .Q(Micro_q), .clk(CLK), .clr(Mic_RST));  // open: load, D, count, carry
  Multiplexer #(.width(8), .enable("false")) multiplexer_1 (
    .in0(Data), .in1({8{1'b1}}), .out(multiplexer_1_out), .sel(d_ff_1_qn));
  Register Inst (.D(multiplexer_1_out), .en(Inst_In), .Q(Inst_q), .clk(CLK));  // open: clr
  not not_1 (not_1_out, d_ff_1_qn);
  not not_2 (not_2_out, Write);
  Register Addr_Hi (.D(ALU_Out), .en(Addr_H_In), .Q(Addr_H_Val), .clk(CLK));  // open: clr
  assign Inst_In = d_ff_1_qn ? d_ff_1_qn : 1'bz;  // Controlled_Buffer controlled_buffer_1
  assign Addr_Out = d_ff_1_qn ? d_ff_1_qn : 1'bz;  // Controlled_Buffer controlled_buffer_2
  assign CNT_En = d_ff_1_qn ? not_1_out : 1'bz;  // Controlled_Buffer controlled_buffer_3
  RAM #(.addrWidth(14)) ram_1 (
    .addr(multiplexer_2_out[13:0]), .data(Data), .sel(nor_1_out), .clk(CLK), .ld(not_2_out), .clr(1'b0));
  ROM #(.addrWidth(15)) rom_1 (.addr(multiplexer_2_out[14:0]), .data(Data), .sel(multiplexer_2_out[15]));
  // Probe on Data
  // Probe on multiplexer_2_out
  nor nor_2 (HLT, Addr_Out, Mic_RST, Cnt_L_In, Cnt_H_In, CNT_En, Inst_In, First_Select, Second_Select[0], Second_Select[1], Second_Select[2], OP_Select[0], OP_Select[1], OP_Select[2], OP_Select[3], ALU_Out_Select[0], ALU_Out_Select[1], Data_Out_Select[0], Data_Out_Select[1], Data_Out_Select[2], Flag_Inst[0], Flag_Inst[1], Flag_Inst[2], Use_C_F[0], Use_C_F[1], CF_En, ZF_En, VF_En, NF_En, rom_2_data[29], rom_2_data[30], rom_2_data[31], ALU_Out_Select[2]);
  Counter #(.trigger("falling")) P_Cnt_Lo (
    .load(Cnt_L_In), .D(Addr_L_Val), .count(CNT_En), .Q(P_Cnt_Lo_q), .carry(P_Cnt_Lo_carry), .clk(CLK));  // open: clr
  ROM #(.addrWidth(16), .dataWidth(32)) rom_2 (
    .addr({Condition, CF, Inst_q, Micro_q}),
    .data({rom_2_data, NF_En, VF_En, ZF_En, CF_En, Use_C_F, Flag_Inst, Data_Out_Select, ALU_Out_Select, OP_Select, Second_Select, First_Select, Inst_In, CNT_En, Cnt_H_In, Cnt_L_In, Mic_RST, Addr_Out}),
    .sel(d_ff_1_q));
  Counter #(.trigger("falling")) P_Cnt_Hi (
    .load(Cnt_H_In), .D(Addr_H_Val), .count(P_Cnt_Lo_carry), .Q(P_Cnt_Hi_q), .clk(CLK));  // open: carry, clr
  assign Data = Cnt_L_Out ? P_Cnt_Lo_q : 8'bz;  // Controlled_Buffer controlled_buffer_4
  nor nor_3 (nor_3_out, multiplexer_2_out[15], multiplexer_2_out[8], multiplexer_2_out[9], multiplexer_2_out[10], multiplexer_2_out[11]);
  Multiplexer #(.width(16), .disabled(0), .enable("false")) multiplexer_2 (
    .in0({P_Cnt_Hi_q, P_Cnt_Lo_q}), .in1({Addr_H_Val, Addr_L_Val}), .out(multiplexer_2_out), .sel(Addr_Out));
  assign Data = Cnt_H_Out ? P_Cnt_Hi_q : 8'bz;  // Controlled_Buffer controlled_buffer_5
  and and_2 (and_2_out, nor_3_out, multiplexer_2_out[12], multiplexer_2_out[13], multiplexer_2_out[14]);
  Decoder #(.select(2), .disabled(0)) decoder_1 (
    .out0(decoder_1_out0), .out1(decoder_1_out1), .out2(decoder_1_out2), .sel(multiplexer_2_out[1:0]),
    .en(and_2_out));  // open: out3
  Decoder #(.select(3), .disabled(0), .enable("false")) decoder_2 (
    .out1(C_Clear), .out2(C_Set), .out3(I_Clear), .out4(I_Set), .out5(V_Clear), .out6(D_Clear), .out7(D_Set),
    .sel(Flag_Inst));  // open: out0
  and and_3 (and_3_out, CLK, decoder_1_out0);
  assign controlled_buffer_6_out = decoder_1_out0 ? Data : 8'bz;  // Controlled_Buffer controlled_buffer_6
  Keyboard keyboard_1 (
    .clk(CLK), .re(decoder_1_out1), .avail(keyboard_1_avail[7]), .data(keyboard_1_data));  // open: clr
  assign Data = decoder_1_out1 ? {keyboard_1_avail[7], keyboard_1_data} : 8'bz;  // Controlled_Buffer controlled_buffer_7
  Random random_1 (.clk(CLK), .next(decoder_1_out2), .out(random_1_out));  // open: clr
  assign Data = decoder_1_out2 ? random_1_out : 8'bz;  // Controlled_Buffer controlled_buffer_8
  NZ nz_1 (.in_1(ALU_Out), .Z(nz_1_z[1]), .N(nz_1_z[7]));
  TTY tty_1 (
    .data(controlled_buffer_6_out[6:0]), .clk(and_3_out), .we(decoder_1_out0),
    .clr(controlled_buffer_6_out[7]));
  Decoder #(.select(3), .disabled(0), .enable("false")) decoder_3 (
    .out0(B_In), .out1(A_In), .out2(X_In), .out3(Y_In), .out4(SP_In), .out5(Addr_H_In), .out6(Addr_L_In),
    .out7(F_In), .sel(ALU_Out_Select));
  Decoder #(.select(3), .disabled(0), .enable("false")) decoder_4 (
    .out0(decoder_4_out0), .out1(A_Out), .out2(B_Out), .out3(Cnt_H_Out), .out4(Cnt_L_Out), .out5(X_Out),
    .out6(Y_Out), .out7(F_Out), .sel(Data_Out_Select));
  Multiplexer #(.select(2), .enable("false")) multiplexer_3 (
    .in0(1'b0), .in1(1'b1), .in2(LCF), .in3(CF), .out(ALU_C_In), .sel(Use_C_F));
  not not_3 (Write, decoder_4_out0);
  Multiplexer #(.width(8), .disabled(0), .enable("false")) multiplexer_4 (
    .in0({nz_1_z[7], 1'b0, ALU_C_Out, 3'b000, nz_1_z[1], ALU_C_Out}), .in1(ALU_Out), .out(multiplexer_4_out),
    .sel(F_In));
  Joystick joystick_1 ();  // open: x, y
  ALU alu_1 (
    .Data(Data), .A(A_Val), .X(X_Val), .Y(Y_Val), .SP(SP_Val), .AddrL(Addr_L_Val), .AddrH(Addr_H_Val),
    .B(B_Val), .C_In(ALU_C_In), .First_select(First_Select), .Second_select(Second_Select),
    .Op_select(OP_Select), .Q(ALU_Out), .C_Out(ALU_C_Out));
  D_Flip_Flop C (
    .clk(CLK), .D(multiplexer_4_out[0]), .Q(CF), .preset(C_Set), .en(or_1_out), .reset(C_Clear));  // open: Qn
  or or_1 (or_1_out, CF_En, F_In);
  D_Flip_Flop Z (.clk(CLK), .D(multiplexer_4_out[1]), .Q(Condition[1]), .en(or_2_out));  // open: Qn, preset, reset
  or or_2 (or_2_out, ZF_En, F_In);
  D_Flip_Flop I (.clk(CLK), .D(multiplexer_4_out[2]), .Q(IF), .preset(I_Set), .en(F_In), .reset(I_Clear));  // open: Qn
  D_Flip_Flop D (.clk(CLK), .D(multiplexer_4_out[3]), .Q(DF), .preset(D_Set), .en(F_In), .reset(D_Clear));  // open: Qn
  D_Flip_Flop B (.clk(CLK), .D(multiplexer_4_out[4]), .Q(BF), .en(F_In));  // open: Qn, preset, reset
  D_Flip_Flop Last_C (.clk(CLK), .D(multiplexer_4_out[5]), .Q(LCF), .en(1'b1));  // open: Qn, preset, reset
  D_Flip_Flop V (
    .clk(CLK), .D(multiplexer_4_out[6]), .Q(Condition[2]), .en(or_3_out), .reset(V_Clear));  // open: Qn, preset
  or or_3 (or_3_out, VF_En, F_In);
  D_Flip_Flop N (.clk(CLK), .D(multiplexer_4_out[7]), .Q(Condition[3]), .en(or_4_out));  // open: Qn, preset, reset
  or or_4 (or_4_out, NF_En, F_In);
  DotMatrix #(.matrixcols(32), .matrixrows(32)) dotmatrix_1 ();  // open: col0, col1, col2, col3, col4, col5, col6, col7, col8, col9, col10, col11, col12, col13, col14, col15, col16, col17, col18, col19, col20, col21, col22, col23, col24, col25, col26, col27, col28, col29, col30, col31
  Register A (.D(ALU_Out), .en(A_In), .Q(A_Val), .clk(CLK));  // open: clr
  Register X (.D(ALU_Out), .en(X_In), .Q(X_Val), .clk(CLK));  // open: clr
  Register Y (.D(ALU_Out), .en(Y_In), .Q(Y_Val), .clk(CLK));  // open: clr
  Register SP (.D(ALU_Out), .en(SP_In), .Q(SP_Val), .clk(CLK));  // open: clr
  Register B_2 (.D(ALU_Out), .en(B_In), .Q(B_Val), .clk(CLK));  // open: clr
  assign Data = A_Out ? A_Val : 8'bz;  // Controlled_Buffer controlled_buffer_9
  assign Data = X_Out ? X_Val : 8'bz;  // Controlled_Buffer controlled_buffer_10
  assign Data = Y_Out ? Y_Val : 8'bz;  // Controlled_Buffer controlled_buffer_11
  assign Data = B_Out ? B_Val : 8'bz;  // Controlled_Buffer controlled_buffer_12
  assign Data = F_Out ? {Condition[3:2], 1'b1, BF, DF, IF, Condition[1], CF} : 8'bz;  // Controlled_Buffer controlled_buffer_13

  // Other names for the same wires on the sheet: Condition[0] = CF; ZF = Condition[1]; VF = Condition[2];
  //   NF = Condition[3]

  // Notes on the sheet:
  //   contents of rom_1 (hex, n*v repeats v):
  //   a9 41 85 22 a9 42 85 35 a9 43 85 2a a9 92 85 4d a9 f0 85 4c a9 93 85 51 a9 b1 85 50 a5 22 8d 0 70 a2
  //   2 b5 33 8d 0 70 a2 79 b5 b1 8d 0 70 ad 2 87 8d 0 70 a2 7 bd 41 87 8d 0 70 a2 97 bd a9 87 8d 0 70 a0
  //   56 b9 15 90 8d 0 70 a0 ff b9 18 91 8d 0 70 a2 8 a1 44 8d 0 70 a0 18 b1 50 8d 0 70 1695*ff 44 69*ff
  //   45 247*ff 46 2090*ff 47 427*ff 48 216*ff 49 216*ff 4a 27698*ff 0 80
  //   contents of rom_2 (hex, n*v repeats v):
  //   256*0 30 8080 2 1869*0 30 14000 18050 20001 2 123*0 30 18050 14050 20001 2 299*0 30 1400c050 2 13*0
  //   30 14000 18150 41 818280 14041 18380 14004041 2 7*0 30 14008050 2 45*0 30 14000 18050 14004041 2
  //   59*0 30 14004050 2 13*0 30 8080 2 45*0 30 18050 14050 14004041 2 59*0 30 14000 18050 41 818280 14041
  //   18380 1a400 1014300 14004041 2 53*0 30 14000 18150 14004041 2 59*0 30 181d0 1014050 14004041 2 59*0
  //   30 18150 1014050 14004041 2 1051*0 20 1c 14 14 14054 18040 c 2 264*0 30 8080 2 1869*0 30 14000 18050
  //   20001 2 123*0 30 18050 14050 20001 2 299*0 30 1400c050 2 13*0 30 14000 18150 41 818280 14041 18380
  //   14004041 2 7*0 30 14008050 2 45*0 30 14000 18050 14004041 2 59*0 30 14004050 2 13*0 30 8080 2 45*0
  //   30 18050 14050 14004041 2 59*0 30 14000 18050 41 818280 14041 18380 1a400 1014300 14004041 2 53*0 30
  //   14000 18150 14004041 2 59*0 30 181d0 1014050 14004041 2 59*0 30 18150 1014050 14004041 2 1051*0 20
  //   1c 14 14 14054 18040 c 2 264*0 30 8080 2 1869*0 30 14000 18050 20001 2 123*0 30 18050 14050 20001 2
  //   299*0 30 1400c050 2 13*0 30 14000 18150 41 818280 14041 18380 14004041 2 7*0 30 14008050 2 45*0 30
  //   14000 18050 14004041 2 59*0 30 14004050 2 13*0 30 8080 2 45*0 30 18050 14050 14004041 2 59*0 30
  //   14000 18050 41 818280 14041 18380 1a400 1014300 14004041 2 53*0 30 14000 18150 14004041 2 59*0 30
  //   181d0 1014050 14004041 2 59*0 30 18150 1014050 14004041 2 1051*0 20 1c 14 14 14054 18040 c 2 264*0
  //   30 8080 2 1869*0 30 14000 18050 20001 2 123*0 30 18050 14050 20001 2 299*0 30 1400c050 2 13*0 30
  //   14000 18150 41 818280 14041 18380 14004041 2 7*0 30 14008050 2 45*0 30 14000 18050 14004041 2 59*0
  //   30 14004050 2 13*0 30 8080 2 45*0 30 18050 14050 14004041 2 59*0 30 14000 18050 41 818280 14041
  //   18380 1a400 1014300 14004041 2 53*0 30 14000 18150 14004041 2 59*0 30 181d0 1014050 14004041 2 59*0
  //   30 18150 1014050 14004041 2 1051*0 20 1c 14 14 14054 18040 c 2 264*0 30 8080 2 1869*0 30 14000 18050
  //   20001 2 123*0 30 18050 14050 20001 2 299*0 30 1400c050 2 13*0 30 14000 18150 41 818280 14041 18380
  //   14004041 2 7*0 30 14008050 2 45*0 30 14000 18050 14004041 2 59*0 30 14004050 2 13*0 30 8080 2 45*0
  //   30 18050 14050 14004041 2 59*0 30 14000 18050 41 818280 14041 18380 1a400 1014300 14004041 2 53*0 30
  //   14000 18150 14004041 2 59*0 30 181d0 1014050 14004041 2 59*0 30 18150 1014050 14004041 2 1051*0 20
  //   1c 14 14 14054 18040 c 2 264*0 30 8080 2 1869*0 30 14000 18050 20001 2 123*0 30 18050 14050 20001 2
  //   299*0 30 1400c050 2 13*0 30 14000 18150 41 818280 14041 18380 14004041 2 7*0 30 14008050 2 45*0 30
  //   14000 18050 14004041 2 59*0 30 14004050 2 13*0 30 8080 2 45*0 30 18050 14050 14004041 2 59*0 30
  //   14000 18050 41 818280 14041 18380 1a400 1014300 14004041 2 53*0 30 14000 18150 14004041 2 59*0 30
  //   181d0 1014050 14004041 2 59*0 30 18150 1014050 14004041 2 1051*0 20 1c 14 14 14054 18040 c 2 264*0
  //   30 8080 2 1869*0 30 14000 18050 20001 2 123*0 30 18050 14050 20001 2 299*0 30 1400c050 2 13*0 30
  //   14000 18150 41 818280 14041 18380 14004041 2 7*0 30 14008050 2 45*0 30 14000 18050 14004041 2 59*0
  //   30 14004050 2 13*0 30 8080 2 45*0 30 18050 14050 14004041 2 59*0 30 14000 18050 41 818280 14041
  //   18380 1a400 1014300 14004041 2 53*0 30 14000 18150 14004041 2 59*0 30 181d0 1014050 14004041 2 59*0
  //   30 18150 1014050 14004041 2 1051*0 20 1c 14 14 14054 18040 c 2 264*0 30 8080 2 1869*0 30 14000 18050
  //   20001 2 123*0 30 18050 14050 20001 2 299*0 30 1400c050 2 13*0 30 14000 18150 41 818280 14041 18380
  //   14004041 2 7*0 30 14008050 2 45*0 30 14000 18050 14004041 2 59*0 30 14004050 2 13*0 30 8080 2 45*0
  //   30 18050 14050 14004041 2 59*0 30 14000 18050 41 818280 14041 18380 1a400 1014300 14004041 2 53*0 30
  //   14000 18150 14004041 2 59*0 30 181d0 1014050 14004041 2 59*0 30 18150 1014050 14004041 2 1051*0 20
  //   1c 14 14 14054 18040 c 2 2136*0 30 14000 18050 20001 2 123*0 30 18050 14050 20001 2 299*0 30
  //   1400c050 2 13*0 30 14000 18150 41 818280 14041 18380 14004041 2 7*0 30 14008050 2 45*0 30 14000
  //   18050 14004041 2 59*0 30 14004050 2 13*0 30 8080 2 45*0 30 18050 14050 14004041 2 59*0 30 14000
  //   18050 41 818280 14041 18380 1a400 1014300 14004041 2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
endmodule

module Monitor_PoC (
  input  [3:0] in_1,
  input  in_2
);

  wire and_1_out, and_2_out, button_1_out, clock_1_out, nor_1_out, ram_1_data;
  wire [1:0] register_1_q;
  wire [3:0] counter_1_q, demultiplexer_1_out0, demultiplexer_1_out1, demultiplexer_1_out2,
       demultiplexer_1_out3, multiplexer_1_out, shift_register_1_q3;

  Button button_1 (.out(button_1_out));
  Clock clock_1 (.out(clock_1_out));
  and and_1 (and_1_out, ~button_1_out, clock_1_out);  // AND_Gate
  Counter #(.width(4), .max('hf)) counter_1 (.Q(counter_1_q), .clk(and_1_out));  // open: load, D, count, carry, clr
  Multiplexer #(.width(4), .enable("false")) multiplexer_1 (
    .in0(counter_1_q), .in1(in_1), .out(multiplexer_1_out), .sel(button_1_out));
  and and_2 (and_2_out, button_1_out, clock_1_out);
  nor nor_1 (nor_1_out, counter_1_q[0], counter_1_q[1], and_1_out);
  RAM #(.addrWidth(4), .dataWidth(1), .bus("separate")) ram_1 (
    .addr(multiplexer_1_out), .din(in_2), .data(ram_1_data), .str(button_1_out), .clk(and_2_out));  // open: sel, ld, clr
  Register #(.width(2)) register_1 (
    .D(counter_1_q[3:2]), .en(nor_1_out), .Q(register_1_q), .clk(and_1_out));  // open: clr
  Shift_Register #(.length(4)) shift_register_1 (
    .shift(1'b1), .in(ram_1_data), .clk(and_1_out), .q0(shift_register_1_q3[3]), .q1(shift_register_1_q3[2]),
    .q2(shift_register_1_q3[1]), .q3(shift_register_1_q3[0]));  // open: out, load, clr, d0, d1, d2, d3
  DotMatrix #(.matrixcols(4), .matrixrows(4), .persist(40)) dotmatrix_1 (
    .col0(demultiplexer_1_out0), .col1(demultiplexer_1_out1), .col2(demultiplexer_1_out2),
    .col3(demultiplexer_1_out3));
  Demultiplexer #(.select(2), .width(4), .disabled(0)) demultiplexer_1 (
    .out0(demultiplexer_1_out0), .out1(demultiplexer_1_out1), .out2(demultiplexer_1_out2),
    .out3(demultiplexer_1_out3), .in(shift_register_1_q3), .sel(register_1_q), .en(nor_1_out));
endmodule

module NZ (
  input  [7:0] in_1,
  output Z,
  output N
);

  nor nor_1 (Z, in_1[3], in_1[0], in_1[1], in_1[2], in_1[4], in_1[5], in_1[6], in_1[7]);

  assign N = in_1[7];
endmodule

module ALU (
  input  C_In,
  input  [7:0] Data,
  input  [7:0] A,
  input  [7:0] X,
  input  [7:0] Y,
  input  [7:0] SP,
  input  [7:0] AddrL,
  input  [7:0] AddrH,
  input  [7:0] B,
  input  First_select,
  input  [2:0] Second_select,
  input  [3:0] Op_select,
  output [7:0] Q,
  output C_Out
);

  wire adder_1_cout, adder_2_cout, subtractor_1_bout;
  wire [7:0] adder_1_out, adder_2_out, and_1_out, multiplexer_1_out, multiplexer_2_out, multiplexer_3_out,
       or_1_out, shifter_1_out, shifter_2_out, shifter_3_out, shifter_4_out, subtractor_1_out, xor_1_out;

  Multiplexer #(.width(8), .enable("false")) multiplexer_1 (
    .in0({8{1'b0}}), .in1(Data), .out(multiplexer_1_out), .sel(First_select));
  Multiplexer #(.width(8), .enable("false")) multiplexer_2 (
    .in0(A), .in1(Data), .out(multiplexer_2_out), .sel(First_select));
  Multiplexer #(.select(3), .width(8), .enable("false")) multiplexer_3 (
    .in0({8{1'b0}}), .in1(A), .in2(X), .in3(Y), .in4(SP), .in5(AddrL), .in6(AddrH), .in7(B),
    .out(multiplexer_3_out), .sel(Second_select));
  Adder adder_1 (.a(multiplexer_1_out), .b(multiplexer_3_out), .out(adder_1_out), .cin(C_In), .cout(adder_1_cout));
  Subtractor subtractor_1 (
    .a(multiplexer_1_out), .b(multiplexer_3_out), .out(subtractor_1_out), .bin(C_In), .bout(subtractor_1_bout));
  assign or_1_out = multiplexer_1_out | multiplexer_3_out;  // OR_Gate or_1, 8 bits wide
  assign and_1_out = multiplexer_1_out & multiplexer_3_out;  // AND_Gate and_1, 8 bits wide
  assign xor_1_out = multiplexer_1_out ^ multiplexer_3_out;  // XOR_Gate xor_1, 8 bits wide
  Shifter shifter_1 (.in(multiplexer_2_out), .\dist (3'b001), .out(shifter_1_out));
  Shifter #(.shift("lr")) shifter_2 (.in(multiplexer_2_out), .\dist (3'b001), .out(shifter_2_out));
  Shifter #(.shift("rl")) shifter_3 (.in(multiplexer_2_out), .\dist (3'b001), .out(shifter_3_out));
  Shifter #(.shift("rr")) shifter_4 (.in(multiplexer_2_out), .\dist (3'b001), .out(shifter_4_out));
  Adder adder_2 (.a(AddrL), .b(Y), .out(adder_2_out), .cin(1'b0), .cout(adder_2_cout));
  Multiplexer #(.select(4), .width(8), .enable("false")) multiplexer_4 (
    .in0(adder_1_out), .in1(subtractor_1_out), .in2(or_1_out), .in3(and_1_out), .in4(xor_1_out),
    .in5(shifter_1_out), .in6(shifter_2_out), .in7(shifter_3_out), .in8(shifter_4_out), .in9(adder_2_out),
    .out(Q), .sel(Op_select));  // open: in10, in11, in12, in13, in14, in15
  Multiplexer #(.select(4), .enable("false")) multiplexer_5 (
    .in0(adder_1_cout), .in1(subtractor_1_bout), .in2(1'b0), .in3(1'b0), .in4(1'b0),
    .in5(multiplexer_2_out[7]), .in6(1'b0), .in7(1'b0), .in8(1'b0), .in9(adder_2_cout), .out(C_Out),
    .sel(Op_select));  // open: in10, in11, in12, in13, in14, in15
endmodule
